// Logisim project regfile.circ as structural Verilog: 1 circuit, main circuit regfile
module regfile (
  input  [4:0] rs1,
  input  [4:0] rs2,
  input  [4:0] rd,
  input  [31:0] Write_Data,
  input  RegWEn,
  input  clk,
  output [31:0] ra,
  output [31:0] sp,
  output [31:0] t0,
  output [31:0] t1,
  output [31:0] t2,
  output [31:0] s0,
  output [31:0] s1,
  output [31:0] a0,
  output [31:0] Read_Data_1,
  output [31:0] Read_Data_2
);

  wire [31:0] out0;

  Register #(.width(32)) reg0 (.D(Write_Data), .en(RegWEn), .clk(clk), .Q(out0));  // open: clr
  Register #(.width(32)) reg1 (.D(Write_Data), .en(RegWEn), .clk(clk), .Q(out0));  // open: clr
  Register #(.width(32)) reg2 (.D(Write_Data), .en(RegWEn), .clk(clk), .Q(out0));  // open: clr
  Register #(.width(32)) reg3 (.D(Write_Data), .en(RegWEn), .clk(clk), .Q(out0));  // open: clr
  Register #(.width(32)) reg4 (.D(Write_Data), .en(RegWEn), .clk(clk), .Q(out0));  // open: clr
  Register #(.width(32)) reg5 (.D(Write_Data), .en(RegWEn), .clk(clk), .Q(out0));  // open: clr
  Register #(.width(32)) reg6 (.D(Write_Data), .en(RegWEn), .clk(clk), .Q(out0));  // open: clr
  Register #(.width(32)) reg7 (.D(Write_Data), .en(RegWEn), .clk(clk), .Q(out0));  // open: clr
  Register #(.width(32)) reg8 (.D(Write_Data), .en(RegWEn), .clk(clk), .Q(out0));  // open: clr
  Register #(.width(32)) reg9 (.D(Write_Data), .en(RegWEn), .clk(clk), .Q(out0));  // open: clr
  Register #(.width(32)) reg10 (.D(Write_Data), .en(RegWEn), .clk(clk), .Q(out0));  // open: clr
  Register #(.width(32)) reg11 (.D(Write_Data), .en(RegWEn), .clk(clk), .Q(out0));  // open: clr
  Register #(.width(32)) reg12 (.D(Write_Data), .en(RegWEn), .clk(clk), .Q(out0));  // open: clr
  Register #(.width(32)) reg13 (.D(Write_Data), .en(RegWEn), .clk(clk), .Q(out0));  // open: clr
  Register #(.width(32)) reg14 (.D(Write_Data), .en(RegWEn), .clk(clk), .Q(out0));  // open: clr
  Register #(.width(32)) reg15 (.D(Write_Data), .en(RegWEn), .clk(clk), .Q(out0));  // open: clr
  Register #(.width(32)) register_1 (.D(Write_Data), .en(RegWEn), .clk(clk), .Q(out0));  // open: clr
  Register #(.width(32)) register_2 (.D(Write_Data), .en(RegWEn), .clk(clk), .Q(out0));  // open: clr
  Register #(.width(32)) register_3 (.D(Write_Data), .en(RegWEn), .clk(clk), .Q(out0));  // open: clr
  Register #(.width(32)) register_4 (.D(Write_Data), .en(RegWEn), .clk(clk), .Q(out0));  // open: clr
  Register #(.width(32)) register_5 (.D(Write_Data), .en(RegWEn), .clk(clk), .Q(out0));  // open: clr
  Register #(.width(32)) register_6 (.D(Write_Data), .en(RegWEn), .clk(clk), .Q(out0));  // open: clr
  Register #(.width(32)) register_7 (.D(Write_Data), .en(RegWEn), .clk(clk), .Q(out0));  // open: clr
  Register #(.width(32)) register_8 (.D(Write_Data), .en(RegWEn), .clk(clk), .Q(out0));  // open: clr
  Register #(.width(32)) register_9 (.D(Write_Data), .en(RegWEn), .clk(clk), .Q(out0));  // open: clr
  Register #(.width(32)) register_10 (.D(Write_Data), .en(RegWEn), .clk(clk), .Q(out0));  // open: clr
  Register #(.width(32)) register_11 (.D(Write_Data), .en(RegWEn), .clk(clk), .Q(out0));  // open: clr
  Register #(.width(32)) register_12 (.D(Write_Data), .en(RegWEn), .clk(clk), .Q(out0));  // open: clr
  Register #(.width(32)) register_13 (.D(Write_Data), .en(RegWEn), .clk(clk), .Q(out0));  // open: clr
  Register #(.width(32)) register_14 (.D(Write_Data), .en(RegWEn), .clk(clk), .Q(out0));  // open: clr
  Register #(.width(32)) register_15 (.D(Write_Data), .en(RegWEn), .clk(clk), .Q(out0));  // open: clr
  Register #(.width(32)) register_16 (.D(Write_Data), .en(RegWEn), .clk(clk), .Q(out0));  // open: clr

  // Other names for the same wires on the sheet: read_data1[31:0] = Read_Data_1; read_data2[31:0] = Read_Data_2;
  //   read_reg1[4:0] = rs1; read_reg2[4:0] = rs2; write_en = RegWEn; write_reg[4:0] = rd

  // Notes on the sheet:
  //   INPUTS to your circuit
  //   DON'T CHANGE THE LOCATIONS OF THE INPUTS AND OUTPUTS!
  //   These are DEBUG/TEST outputs from your circuit.
  //   OUTPUTS from your circuit
endmodule
